// Logisim project NoC.circ as structural Verilog: 4 circuits, main circuit Roteador
module Roteador (
  input  Entrada_Norte,
  input  Entrada_Sul,
  input  [1:0] Seletor_Local,
  input  Entrada_Leste,
  input  Entrada_Oeste,
  input  [1:0] Seletor_Norte,
  input  Entrada_Local,
  input  [1:0] Seletor_Sul,
  input  [1:0] Seletor_Leste,
  input  [1:0] Seletor_Oeste,
  output \Saída_Local ,
  output \Saída_Norte ,
  output \Saída_Sul ,
  output \Saída_Leste ,
  output \Saída_Oeste 
);

  wire Buffer_2_out, Buffer_3_out, Buffer_4_out, Buffer_5_out, Buffer_out;

  Controlled_Buffer Buffer (.in(Entrada_Norte), .out(Buffer_out));  // open: en
  Controlled_Buffer Buffer_2 (.in(Entrada_Sul), .out(Buffer_2_out));  // open: en
  Controlled_Buffer Buffer_3 (.in(Entrada_Leste), .out(Buffer_3_out));  // open: en
  Controlled_Buffer Buffer_4 (.in(Entrada_Oeste), .out(Buffer_4_out));  // open: en
  Controlled_Buffer Buffer_5 (.in(Entrada_Local), .out(Buffer_5_out));  // open: en
  Multiplexer #(.select(2), .enable("false")) multiplexer_1 (
    .in0(Buffer_out), .in1(Buffer_2_out), .in2(Buffer_3_out), .in3(Buffer_4_out), .out(\Saída_Local ),
    .sel(Seletor_Local));
  Multiplexer #(.select(2), .enable("false")) multiplexer_2 (
    .in0(Buffer_5_out), .in1(Buffer_2_out), .in2(Buffer_3_out), .in3(Buffer_4_out), .out(\Saída_Norte ),
    .sel(Seletor_Norte));
  Multiplexer #(.select(2), .enable("false")) multiplexer_3 (
    .in0(Buffer_5_out), .in1(Buffer_out), .in2(Buffer_3_out), .in3(Buffer_4_out), .out(\Saída_Sul ),
    .sel(Seletor_Sul));
  Multiplexer #(.select(2), .enable("false")) multiplexer_4 (
    .in0(Buffer_5_out), .in1(Buffer_out), .in2(Buffer_2_out), .in3(Buffer_4_out), .out(\Saída_Leste ),
    .sel(Seletor_Leste));
  Multiplexer #(.select(2), .enable("false")) multiplexer_5 (
    .in0(Buffer_5_out), .in1(Buffer_out), .in2(Buffer_2_out), .in3(Buffer_3_out), .out(\Saída_Oeste ),
    .sel(Seletor_Oeste));
endmodule

module \Núcleo  (
  input  Entrada_Local,
  output \Saída_Local 
);
endmodule

module Middleware (
  output [1:0] Seletor_Local,
  output [1:0] Seletor_Norte,
  output [1:0] Seletor_Sul,
  output [1:0] Seletor_Leste,
  output [1:0] Seletor_Oeste,
  output [1:0] Seletor_Local_2,
  output [1:0] Seletor_Norte_2,
  output [1:0] Seletor_Sul_2,
  output [1:0] Seletor_Leste_2,
  output [1:0] Seletor_Oeste_2,
  output [1:0] Seletor_Local_3,
  output [1:0] Seletor_Norte_3,
  output [1:0] Seletor_Sul_3,
  output [1:0] Seletor_Leste_3,
  output [1:0] Seletor_Oeste_3,
  output [1:0] Seletor_Local_4,
  output [1:0] Seletor_Local_5,
  output [1:0] Seletor_Norte_4,
  output [1:0] Seletor_Norte_5,
  output [1:0] Seletor_Sul_4,
  output [1:0] Seletor_Sul_5,
  output [1:0] Seletor_Leste_4,
  output [1:0] Seletor_Leste_5,
  output [1:0] Seletor_Oeste_4,
  output [1:0] Seletor_Oeste_5,
  output [1:0] Seletor_Local_6,
  output [1:0] Seletor_Norte_6,
  output [1:0] Seletor_Sul_6,
  output [1:0] Seletor_Leste_6,
  output [1:0] Seletor_Oeste_6,
  output [1:0] Seletor_Local_7,
  output [1:0] Seletor_Norte_7,
  output [1:0] Seletor_Sul_7,
  output [1:0] Seletor_Leste_7,
  output [1:0] Seletor_Oeste_7,
  output [1:0] Seletor_Local_8,
  output [1:0] Seletor_Norte_8,
  output [1:0] Seletor_Sul_8,
  output [1:0] Seletor_Leste_8,
  output [1:0] Seletor_Oeste_8
);
endmodule

module NoC (
);

  wire \núcleo_1_saída_local , \núcleo_2_saída_local , \núcleo_3_saída_local , \núcleo_4_saída_local ,
       \núcleo_5_saída_local , \núcleo_6_saída_local , \núcleo_7_saída_local , \núcleo_8_saída_local ,
       \roteador_1_saída_local , \roteador_1_saída_oeste , \roteador_1_saída_sul , \roteador_2_saída_local ,
       \roteador_2_saída_norte , \roteador_2_saída_sul , \roteador_3_saída_local , \roteador_3_saída_norte ,
       \roteador_3_saída_oeste , \roteador_4_saída_leste , \roteador_4_saída_local ,
       \roteador_4_saída_oeste , \roteador_5_saída_leste , \roteador_5_saída_local ,
       \roteador_5_saída_oeste , \roteador_6_saída_leste , \roteador_6_saída_local , \roteador_6_saída_sul ,
       \roteador_7_saída_local , \roteador_7_saída_norte , \roteador_7_saída_sul , \roteador_8_saída_leste ,
       \roteador_8_saída_local , \roteador_8_saída_norte ;
  wire [1:0] middleware_1_seletor_leste, middleware_1_seletor_leste_2, middleware_1_seletor_leste_3,
       middleware_1_seletor_leste_4, middleware_1_seletor_leste_5, middleware_1_seletor_leste_6,
       middleware_1_seletor_leste_7, middleware_1_seletor_leste_8, middleware_1_seletor_local,
       middleware_1_seletor_local_2, middleware_1_seletor_local_3, middleware_1_seletor_local_4,
       middleware_1_seletor_local_5, middleware_1_seletor_local_6, middleware_1_seletor_local_7,
       middleware_1_seletor_local_8, middleware_1_seletor_norte, middleware_1_seletor_norte_2,
       middleware_1_seletor_norte_3, middleware_1_seletor_norte_4, middleware_1_seletor_norte_5,
       middleware_1_seletor_norte_6, middleware_1_seletor_norte_7, middleware_1_seletor_norte_8,
       middleware_1_seletor_oeste, middleware_1_seletor_oeste_2, middleware_1_seletor_oeste_3,
       middleware_1_seletor_oeste_4, middleware_1_seletor_oeste_5, middleware_1_seletor_oeste_6,
       middleware_1_seletor_oeste_7, middleware_1_seletor_oeste_8, middleware_1_seletor_sul,
       middleware_1_seletor_sul_2, middleware_1_seletor_sul_3, middleware_1_seletor_sul_4,
       middleware_1_seletor_sul_5, middleware_1_seletor_sul_6, middleware_1_seletor_sul_7,
       middleware_1_seletor_sul_8;

  \Núcleo  \núcleo_1  (.Entrada_Local(\roteador_1_saída_local ), .\Saída_Local (\núcleo_1_saída_local ));
  \Núcleo  \núcleo_2  (.Entrada_Local(\roteador_2_saída_local ), .\Saída_Local (\núcleo_2_saída_local ));
  \Núcleo  \núcleo_3  (.Entrada_Local(\roteador_3_saída_local ), .\Saída_Local (\núcleo_3_saída_local ));
  Roteador roteador_1 (
    .Entrada_Local(\núcleo_1_saída_local ), .\Saída_Local (\roteador_1_saída_local ),
    .Entrada_Sul(\roteador_2_saída_norte ), .Seletor_Local(middleware_1_seletor_local),
    .Seletor_Norte(middleware_1_seletor_norte), .Seletor_Sul(middleware_1_seletor_sul),
    .Seletor_Leste(middleware_1_seletor_leste), .Seletor_Oeste(middleware_1_seletor_oeste),
    .\Saída_Sul (\roteador_1_saída_sul ), .Entrada_Oeste(\roteador_4_saída_leste ),
    .\Saída_Oeste (\roteador_1_saída_oeste ));  // open: Entrada_Leste, Saída_Leste, Entrada_Norte, Saída_Norte
  Roteador roteador_2 (
    .Entrada_Norte(\roteador_1_saída_sul ), .Entrada_Local(\núcleo_2_saída_local ),
    .\Saída_Local (\roteador_2_saída_local ), .\Saída_Norte (\roteador_2_saída_norte ),
    .Entrada_Sul(\roteador_3_saída_norte ), .Seletor_Local(middleware_1_seletor_local_4),
    .Seletor_Norte(middleware_1_seletor_norte_4), .Seletor_Sul(middleware_1_seletor_sul_4),
    .Seletor_Leste(middleware_1_seletor_leste_4), .Seletor_Oeste(middleware_1_seletor_oeste_4),
    .\Saída_Sul (\roteador_2_saída_sul ));  // open: Entrada_Leste, Saída_Leste, Entrada_Oeste, Saída_Oeste
  Roteador roteador_3 (
    .Entrada_Norte(\roteador_2_saída_sul ), .Entrada_Local(\núcleo_3_saída_local ),
    .\Saída_Local (\roteador_3_saída_local ), .\Saída_Norte (\roteador_3_saída_norte ),
    .Seletor_Local(middleware_1_seletor_local_6), .Seletor_Norte(middleware_1_seletor_norte_6),
    .Seletor_Sul(middleware_1_seletor_sul_6), .Seletor_Leste(middleware_1_seletor_leste_6),
    .Seletor_Oeste(middleware_1_seletor_oeste_6), .Entrada_Oeste(\roteador_5_saída_leste ),
    .\Saída_Oeste (\roteador_3_saída_oeste ));  // open: Entrada_Leste, Saída_Leste, Entrada_Sul, Saída_Sul
  \Núcleo  \núcleo_4  (.Entrada_Local(\roteador_4_saída_local ), .\Saída_Local (\núcleo_4_saída_local ));
  \Núcleo  \núcleo_5  (.Entrada_Local(\roteador_5_saída_local ), .\Saída_Local (\núcleo_5_saída_local ));
  Roteador roteador_4 (
    .Entrada_Leste(\roteador_1_saída_oeste ), .\Saída_Leste (\roteador_4_saída_leste ),
    .Entrada_Local(\núcleo_4_saída_local ), .\Saída_Local (\roteador_4_saída_local ),
    .Seletor_Local(middleware_1_seletor_local_2), .Seletor_Norte(middleware_1_seletor_norte_2),
    .Seletor_Sul(middleware_1_seletor_sul_2), .Seletor_Leste(middleware_1_seletor_leste_2),
    .Seletor_Oeste(middleware_1_seletor_oeste_2), .Entrada_Oeste(\roteador_6_saída_leste ),
    .\Saída_Oeste (\roteador_4_saída_oeste ));  // open: Entrada_Norte, Saída_Norte, Entrada_Sul, Saída_Sul
  Middleware middleware_1 (
    .Seletor_Local_4(middleware_1_seletor_local_4), .Seletor_Norte_4(middleware_1_seletor_norte_4),
    .Seletor_Sul_4(middleware_1_seletor_sul_4), .Seletor_Leste_4(middleware_1_seletor_leste_4),
    .Seletor_Oeste_4(middleware_1_seletor_oeste_4), .Seletor_Local(middleware_1_seletor_local),
    .Seletor_Local_2(middleware_1_seletor_local_2), .Seletor_Local_3(middleware_1_seletor_local_3),
    .Seletor_Norte(middleware_1_seletor_norte), .Seletor_Norte_2(middleware_1_seletor_norte_2),
    .Seletor_Norte_3(middleware_1_seletor_norte_3), .Seletor_Sul(middleware_1_seletor_sul),
    .Seletor_Sul_2(middleware_1_seletor_sul_2), .Seletor_Sul_3(middleware_1_seletor_sul_3),
    .Seletor_Leste(middleware_1_seletor_leste), .Seletor_Leste_2(middleware_1_seletor_leste_2),
    .Seletor_Leste_3(middleware_1_seletor_leste_3), .Seletor_Oeste(middleware_1_seletor_oeste),
    .Seletor_Oeste_2(middleware_1_seletor_oeste_2), .Seletor_Oeste_3(middleware_1_seletor_oeste_3),
    .Seletor_Local_6(middleware_1_seletor_local_6), .Seletor_Local_7(middleware_1_seletor_local_7),
    .Seletor_Local_8(middleware_1_seletor_local_8), .Seletor_Norte_6(middleware_1_seletor_norte_6),
    .Seletor_Norte_7(middleware_1_seletor_norte_7), .Seletor_Norte_8(middleware_1_seletor_norte_8),
    .Seletor_Sul_6(middleware_1_seletor_sul_6), .Seletor_Sul_7(middleware_1_seletor_sul_7),
    .Seletor_Sul_8(middleware_1_seletor_sul_8), .Seletor_Leste_6(middleware_1_seletor_leste_6),
    .Seletor_Leste_7(middleware_1_seletor_leste_7), .Seletor_Leste_8(middleware_1_seletor_leste_8),
    .Seletor_Oeste_6(middleware_1_seletor_oeste_6), .Seletor_Oeste_7(middleware_1_seletor_oeste_7),
    .Seletor_Oeste_8(middleware_1_seletor_oeste_8), .Seletor_Local_5(middleware_1_seletor_local_5),
    .Seletor_Norte_5(middleware_1_seletor_norte_5), .Seletor_Sul_5(middleware_1_seletor_sul_5),
    .Seletor_Leste_5(middleware_1_seletor_leste_5), .Seletor_Oeste_5(middleware_1_seletor_oeste_5));
  Roteador roteador_5 (
    .Entrada_Leste(\roteador_3_saída_oeste ), .\Saída_Leste (\roteador_5_saída_leste ),
    .Entrada_Local(\núcleo_5_saída_local ), .\Saída_Local (\roteador_5_saída_local ),
    .Seletor_Local(middleware_1_seletor_local_7), .Seletor_Norte(middleware_1_seletor_norte_7),
    .Seletor_Sul(middleware_1_seletor_sul_7), .Seletor_Leste(middleware_1_seletor_leste_7),
    .Seletor_Oeste(middleware_1_seletor_oeste_7), .Entrada_Oeste(\roteador_8_saída_leste ),
    .\Saída_Oeste (\roteador_5_saída_oeste ));  // open: Entrada_Norte, Saída_Norte, Entrada_Sul, Saída_Sul
  \Núcleo  \núcleo_6  (.Entrada_Local(\roteador_6_saída_local ), .\Saída_Local (\núcleo_6_saída_local ));
  Roteador roteador_6 (
    .Entrada_Leste(\roteador_4_saída_oeste ), .\Saída_Leste (\roteador_6_saída_leste ),
    .Entrada_Local(\núcleo_6_saída_local ), .\Saída_Local (\roteador_6_saída_local ),
    .Entrada_Sul(\roteador_7_saída_norte ), .Seletor_Local(middleware_1_seletor_local_3),
    .Seletor_Norte(middleware_1_seletor_norte_3), .Seletor_Sul(middleware_1_seletor_sul_3),
    .Seletor_Leste(middleware_1_seletor_leste_3), .Seletor_Oeste(middleware_1_seletor_oeste_3),
    .\Saída_Sul (\roteador_6_saída_sul ));  // open: Entrada_Norte, Saída_Norte, Entrada_Oeste, Saída_Oeste
  Roteador roteador_7 (
    .Entrada_Norte(\roteador_6_saída_sul ), .Entrada_Local(\núcleo_7_saída_local ),
    .\Saída_Local (\roteador_7_saída_local ), .\Saída_Norte (\roteador_7_saída_norte ),
    .Entrada_Sul(\roteador_8_saída_norte ), .Seletor_Local(middleware_1_seletor_local_5),
    .Seletor_Norte(middleware_1_seletor_norte_5), .Seletor_Sul(middleware_1_seletor_sul_5),
    .Seletor_Leste(middleware_1_seletor_leste_5), .Seletor_Oeste(middleware_1_seletor_oeste_5),
    .\Saída_Sul (\roteador_7_saída_sul ));  // open: Entrada_Leste, Saída_Leste, Entrada_Oeste, Saída_Oeste
  Roteador roteador_8 (
    .Entrada_Leste(\roteador_5_saída_oeste ), .\Saída_Leste (\roteador_8_saída_leste ),
    .Entrada_Norte(\roteador_7_saída_sul ), .Entrada_Local(\núcleo_8_saída_local ),
    .\Saída_Local (\roteador_8_saída_local ), .\Saída_Norte (\roteador_8_saída_norte ),
    .Seletor_Local(middleware_1_seletor_local_8), .Seletor_Norte(middleware_1_seletor_norte_8),
    .Seletor_Sul(middleware_1_seletor_sul_8), .Seletor_Leste(middleware_1_seletor_leste_8),
    .Seletor_Oeste(middleware_1_seletor_oeste_8));  // open: Entrada_Sul, Saída_Sul, Entrada_Oeste, Saída_Oeste
  \Núcleo  \núcleo_7  (.Entrada_Local(\roteador_7_saída_local ), .\Saída_Local (\núcleo_7_saída_local ));
  \Núcleo  \núcleo_8  (.Entrada_Local(\roteador_8_saída_local ), .\Saída_Local (\núcleo_8_saída_local ));
endmodule
